# Fritzing sketch oofGrifBoxThermoCouple (saved by Fritzing 0.8.7b)

parts:
  PanelThermoCouple = MAX31855 Breakout Board with Thermocouple
  EnvironmentThermoCouple = MAX31855 Breakout Board with Thermocouple
  Componente2 = Arduino Mega 2560 (Rev3)

nets:
  VIN: PanelThermoCouple.Vin, EnvironmentThermoCouple.Vin, Componente2.5V
  GND: PanelThermoCouple.GND, EnvironmentThermoCouple.GND, Componente2.GND
  N1: PanelThermoCouple.DO, Componente2.D23
  N2: PanelThermoCouple.CS, Componente2.D25
  N3: PanelThermoCouple.CLK, Componente2.D27
  N4: EnvironmentThermoCouple.DO, Componente2.D22
  N5: EnvironmentThermoCouple.CS, Componente2.D24
  N6: EnvironmentThermoCouple.CLK, Componente2.D26

notes:
  Adafruit Panel Thermocouple:
  D0 must be connected to Pin 23.
  CS must be connected to Pin 25.
  CLK must be connected to Pin 27.
  Vin can be connected to any 5V pin and Gnd to any Gnd Pin.
  Adafruit Environment Thermocouple:
  D0 must be connected to Pin 22.
  CS must be connected to Pin 24.
  CLK must be connected to Pin 26.
  Vin can be connected to any 5V pin and Gnd to any Gnd Pin.
